# Fritzing sketch BASURA (saved by Fritzing 0.9.3b)
breadboards: 1

parts:
  R1 = Resistor [tolerance=±5% resistance=300 package=THT]
  R2 = Resistor [tolerance=±5% resistance=330 package=THT]
  R3 = Resistor [tolerance=±5% resistance=300 package=THT]
  R4 = Resistor [tolerance=±5% resistance=300 package=THT]
  R5 = Rotary Potentiometer (Small) [maximum_resistance=100kΩ package=THT]
  Componente1 = Arduino Uno (Rev3)
  LED2 = smd LED [color="Green (555nm)" package="0603 [SMD]"]
  LED3 = smd LED [color="Blue (430nm)" package="0603 [SMD]"]
  LED4 = smd LED [color="Red (633nm)" package="0603 [SMD]"]
  LED1 = smd LED [color="Yellow (595nm)" package="0805 [SMD]"]
  LED1_2 = smd LED [color="Yellow (585nm)" package="0603 [SMD]"]
  T1 = LM35 Temperature Sensor [package="TO92 [THT]"]
  hc-sr1 = hc-sr04
  U2 = LCD-16X2 BACK [package=lcd-16x2]
  VCC1 = Battery  # not connected
  J1 = Basic Servo

nets:
  5V: R1.Pin_0, R2.Pin_0, R3.Pin_0, R4.Pin_0, R5.leg1, Componente1.5V, T1.+Vs, hc-sr1.VCC
  N1: R1.Pin_1, LED3.anode
  N2: R2.Pin_1, LED2.anode
  N3: R3.Pin_1, LED1.anode, LED1_2.anode
  N4: R4.Pin_1, LED4.anode
  N5: R5.wiper, U2.VO
  GND: R5.leg2, Componente1.GND, T1.GND, hc-sr1.GND, U2.VSS
  N6: Componente1.A5/SCL, T1.Vout
  N7: Componente1.D8, U2.DB7
  N8: Componente1.D9_PWM, U2.DB6
  N9: Componente1.D10_PWM/SS, U2.DB5
  N10: Componente1.D11_PWM/MOSI, U2.DB4
  N11: Componente1.D12/MISO, U2.E
  N12: Componente1.D13/SCK, U2.RS
  N13: Componente1.D0/RX, LED3.cathode
  N14: Componente1.D1/TX, hc-sr1.Trig
  N15: Componente1.D2, hc-sr1.Echo
  N16: Componente1.D3_PWM, J1.pulse
  N17: Componente1.D4, LED2.cathode
  N18: Componente1.D5_PWM, LED1.cathode
  N19: Componente1.D7, LED4.cathode
  N20: U2.VDD, U2.A
  N21: U2.R_W, U2.K

custom parts:
  LCD-16X2 BACK: Standard text-only 16x2 parallel input LCD
