# Fritzing sketch BASURA2 (saved by Fritzing 0.9.3b)
breadboards: 1

parts:
  R1 = Resistor [tolerance=±5% resistance=300 package=THT]
  R2 = Resistor [tolerance=±5% resistance=330 package=THT]
  R3 = Resistor [tolerance=±5% resistance=300 package=THT]
  R4 = Resistor [tolerance=±5% resistance=300 package=THT]
  LED2 = smd LED [color="Green (555nm)" package="0603 [SMD]"]
  LED3 = smd LED [color="Blue (430nm)" package="0603 [SMD]"]
  LED4 = smd LED [color="Red (633nm)" package="0603 [SMD]"]
  LED1 = smd LED [color="Yellow (595nm)" package="0805 [SMD]"]
  U2 = LCD-16X2 BACK [package=lcd-16x2]
  Componente1 = Arduino Mega 2560 (Rev3)
  R6 = Rotary Potentiometer (Small) [package=THT]
  T2 = LM35 Temperature Sensor [package="TO92 [THT]"]
  hc-sr2 = hc-sr04
  J2 = Basic Servo

nets:
  N1: R1.Pin_0, LED1.cathode
  GND: R1.Pin_1, R2.Pin_1, R3.Pin_1, R4.Pin_1, U2.VSS, U2.R_W, U2.K, Componente1.GND, R6.gnd, T2.GND, hc-sr2.GND, J2.gnd
  N2: R2.Pin_0, LED3.cathode
  N3: R3.Pin_0, LED2.cathode
  N4: R4.Pin_0, LED4.cathode
  N5: LED2.anode, Componente1.D25
  N6: LED3.anode, Componente1.D53
  N7: LED4.anode, Componente1.5V
  N8: LED1.anode, Componente1.D23
  VCC: U2.VDD, U2.A, hc-sr2.VCC, J2.vcc
  N9: U2.VO, R6.out
  N10: U2.RS, Componente1.D32
  N11: U2.E, Componente1.D30
  N12: U2.DB4, Componente1.D28
  N13: U2.DB5, Componente1.D26
  N14: U2.DB6, Componente1.D24
  N15: U2.DB7, Componente1.D22
  N16: Componente1.A0, T2.Vout
  N17: Componente1.D27, hc-sr2.Trig
  N18: Componente1.D29, hc-sr2.Echo

custom parts:
  LCD-16X2 BACK: Standard text-only 16x2 parallel input LCD
  Rotary Potentiometer (Small): A rotary adjustable resistor (potentiometer).
